// Logisim project SingleCycle_t_6.circ as structural Verilog: 8 circuits, main circuit DataPath
module ALU (
  input  [4:0] OpCode,
  input  [23:0] BusA,
  input  [23:0] BusB,
  output Zero,
  output [23:0] Result,
  output Branch
);

  wire ADD, ADDI, AND, ANDI, BEQ, CAS, CMP, EQ, GT, JR, LT, LW, LWS, or_1_out, or_2_out, SUB, SW;
  wire [1:0] priority_encoder_1_out;
  wire [23:0] adder_1_out, and_1_out, multiplexer_1_out, subtractor_1_out;

  Decoder #(.select(5), .enable("false")) decoder_1 (
    .out0(AND), .out1(CAS), .out2(LWS), .out3(ADD), .out4(SUB), .out5(CMP), .out6(JR), .out7(ANDI),
    .out8(ADDI), .out9(LW), .out10(SW), .out11(BEQ), .sel(OpCode));  // open: out12, out13, out14, out15, out16, out17, out18, out19, out20, out21, out22, out23, out24, out25, out26, out27, out28, out29, out30, out31
  Adder #(.width(24)) adder_1 (.a(BusA), .b(BusB), .out(adder_1_out));  // open: cin, cout
  Subtractor #(.width(24)) subtractor_1 (.a(BusA), .b(BusB), .out(subtractor_1_out));  // open: bin, bout
  Comparator #(.width(24)) comparator_1 (.a(BusA), .b(BusB), .gt(GT), .eq(EQ), .lt(LT));
  Priority_Encoder #(.select(2)) priority_encoder_1 (
    .in0(GT), .in1(EQ), .in2(LT), .out(priority_encoder_1_out), .en_in(1'b1));  // open: in3, gs, en_out
  or or_1 (or_1_out, LWS, ADD, ADDI, LW, SW);
  or or_2 (or_2_out, AND, ANDI);
  assign and_1_out = BusA & BusB;  // AND_Gate and_1, 24 bits wide
  assign Result = or_2_out ? and_1_out : 24'bz;  // Controlled_Buffer controlled_buffer_1
  assign Result = or_1_out ? adder_1_out : 24'bz;  // Controlled_Buffer controlled_buffer_2
  assign Result = SUB ? subtractor_1_out : 24'bz;  // Controlled_Buffer controlled_buffer_3
  Multiplexer #(.select(2), .width(24), .enable("false")) multiplexer_1 (
    .in0(BusA), .in1(BusA), .in2(BusB), .out(multiplexer_1_out), .sel(priority_encoder_1_out));  // open: in3
  assign Result = CAS ? multiplexer_1_out : 24'bz;  // Controlled_Buffer controlled_buffer_4
  assign Zero = SUB ? EQ : 1'bz;  // Controlled_Buffer controlled_buffer_5
  assign Zero = CMP ? LT : 1'bz;  // Controlled_Buffer controlled_buffer_6
  assign Branch = BEQ ? EQ : 1'bz;  // Controlled_Buffer controlled_buffer_7
endmodule

module ControlUnit (
  input  SF,
  input  [4:0] OpCode,
  input  zero,
  input  [1:0] cond,
  output MemRD,
  output ALUSrc,
  output [1:0] WBData,
  output [1:0] RegDst,
  output RegWr,
  output RegSrc,
  output [1:0] PCSrc,
  output ExtOp,
  output MemWR,
  output ZeroEN
);

  wire ADD, ADDI, AND, and_1_out, and_5_out, and_6_out, and_7_out, and_8_out, ANDI, BEQ, CAS, CMP, Execute,
       J, JR, LW, LWS, nor_1_out, not_1_out, or_1_out, SUB, SW;

  Decoder #(.select(5), .enable("false")) decoder_1 (
    .out0(AND), .out1(CAS), .out2(LWS), .out3(ADD), .out4(SUB), .out5(CMP), .out6(JR), .out7(ANDI),
    .out8(ADDI), .out9(LW), .out10(SW), .out11(BEQ), .out12(J), .out13(RegDst[1]), .out14(RegDst[0]),
    .sel(OpCode));  // open: out15, out16, out17, out18, out19, out20, out21, out22, out23, out24, out25, out26, out27, out28, out29, out30, out31
  not not_1 (not_1_out, zero);
  Multiplexer #(.select(2), .enable("false")) multiplexer_1 (
    .in0(1'b1), .in1(zero), .in2(not_1_out), .in3(1'b1), .out(Execute), .sel(cond));
  or or_1 (or_1_out, LW, LWS);
  nor nor_1 (nor_1_out, CMP, JR, SW, BEQ, J);
  not not_2 (ExtOp, ANDI);
  and and_1 (and_1_out, SF, SUB);
  and and_2 (MemRD, Execute, or_1_out);
  and and_3 (RegWr, Execute, nor_1_out);
  or or_2 (ZeroEN, CMP, and_1_out);
  or or_3 (ALUSrc, ANDI, ADDI, LW, SW);
  or or_4 (RegSrc, BEQ, SW);
  and and_4 (MemWR, SW, Execute);
  and and_5 (and_5_out, Execute, JR);
  and and_6 (and_6_out, Execute, BEQ);
  and and_7 (and_7_out, Execute, RegDst[1]);
  and and_8 (and_8_out, Execute, J);
  or or_5 (WBData[0], LW, RegDst[0], LWS);
  or or_6 (WBData[1], RegDst[0], RegDst[1]);
  nor nor_2 (PCSrc[0], and_5_out, and_6_out);
  nor nor_3 (PCSrc[1], and_5_out, and_7_out, and_8_out);

  // Other names for the same wires on the sheet: LUI = RegDst[0]; JAL = RegDst[1]
endmodule

module DataPath (
);

  wire alu_1_branch, alu_1_zero, ALUSrc, clk_out, ExtOp, MemRD, MemWR, RegSrc, RegWr, Zero, ZeroEN;
  wire [1:0] PCSrc, RegDst, WBData;
  wire [2:0] multiplexer_2_out, multiplexer_3_out;
  wire [23:0] adder_1_out, adder_2_out, alu_1_result, datamemory_1_dataout, extender_1_dataout,
       extender_17_1_dataout, instructionmemory_1_instruction, multiplexer_1_out, multiplexer_4_out,
       multiplexer_5_out, multiplexer_6_out, multiplier_1_out, multiplier_2_out, multiplier_3_out,
       register_1_q, registerfile_1_busa, registerfile_1_busb, shifter_1_out;

  Clock clk (.out(clk_out));
  Register #(.width(24)) register_1 (.D(multiplexer_1_out), .Q(register_1_q), .clk(clk_out));  // open: en, clr
  Multiplexer #(.select(2), .width(24), .enable("false")) multiplexer_1 (
    .in0(multiplier_2_out), .in1({register_1_q[23:19], multiplier_1_out[18:0]}), .in2(multiplexer_5_out),
    .in3(adder_1_out), .out(multiplexer_1_out), .sel(PCSrc));
  Adder #(.width(24)) adder_1 (.a(24'h3), .b(register_1_q), .out(adder_1_out));  // open: cin, cout
  InstructionMemory instructionmemory_1 (
    .Address(register_1_q), .clk(clk_out), .Instruction(instructionmemory_1_instruction));
  // Probe on instructionmemory_1_instruction
  Extender_17 extender_17_1 (.DataIn(instructionmemory_1_instruction[16:0]), .DataOut(extender_17_1_dataout));
  Multiplexer #(.width(3), .enable("false")) multiplexer_2 (
    .in0(instructionmemory_1_instruction[9:7]), .in1(instructionmemory_1_instruction[15:13]),
    .out(multiplexer_2_out), .sel(RegSrc));
  Multiplexer #(.select(2), .width(3), .enable("false")) multiplexer_3 (
    .in0(instructionmemory_1_instruction[15:13]), .in1(3'b001), .in2(3'b111), .out(multiplexer_3_out),
    .sel(RegDst));  // open: in3
  Multiplier #(.width(24)) multiplier_1 (
    .a(24'h3), .b(extender_17_1_dataout), .out(multiplier_1_out));  // open: cin, cout
  Extender extender_1 (.DataIn(instructionmemory_1_instruction[9:0]), .ExtOp(ExtOp), .DataOut(extender_1_dataout));
  RegisterFile registerfile_1 (
    .BusW(multiplexer_6_out), .RA(instructionmemory_1_instruction[12:10]), .RW(multiplexer_3_out),
    .RB(multiplexer_2_out), .RegWR(RegWr), .clk(clk_out), .BusA(registerfile_1_busa),
    .BusB(registerfile_1_busb));
  ControlUnit controlunit_1 (
    .OpCode(instructionmemory_1_instruction[21:17]), .RegDst(RegDst), .ALUSrc(ALUSrc), .WBData(WBData),
    .ExtOp(ExtOp), .MemWR(MemWR), .PCSrc(PCSrc), .RegSrc(RegSrc), .zero(Zero),
    .cond(instructionmemory_1_instruction[23:22]), .RegWr(RegWr), .MemRD(MemRD), .ZeroEN(ZeroEN),
    .SF(instructionmemory_1_instruction[16]));
  Multiplier #(.width(24)) multiplier_2 (
    .a(24'h3), .b(registerfile_1_busa), .out(multiplier_2_out));  // open: cin, cout
  Multiplier #(.width(24)) multiplier_3 (.a(24'h3), .b(extender_1_dataout), .out(multiplier_3_out));  // open: cin, cout
  Multiplexer #(.width(24), .enable("false")) multiplexer_4 (
    .in0(registerfile_1_busb), .in1(extender_1_dataout), .out(multiplexer_4_out), .sel(ALUSrc));
  Adder #(.width(24)) adder_2 (.a(adder_1_out), .b(multiplier_3_out), .out(adder_2_out));  // open: cin, cout
  ALU alu_1 (
    .OpCode(instructionmemory_1_instruction[21:17]), .BusA(registerfile_1_busa), .BusB(multiplexer_4_out),
    .Zero(alu_1_zero), .Result(alu_1_result), .Branch(alu_1_branch));
  Multiplexer #(.width(24), .enable("false")) multiplexer_5 (
    .in0(adder_1_out), .in1(adder_2_out), .out(multiplexer_5_out), .sel(alu_1_branch));
  Register #(.width(1)) register_2 (.D(alu_1_zero), .en(ZeroEN), .Q(Zero), .clk(clk_out));  // open: clr
  Shifter #(.width(24)) shifter_1 (.in(extender_17_1_dataout), .\dist (5'b00100), .out(shifter_1_out));
  // Probe on multiplexer_6_out
  DataMemory datamemory_1 (
    .Address(alu_1_result), .DataIn(registerfile_1_busb), .clk(clk_out), .MemRD(MemRD), .MemWR(MemWR),
    .DataOut(datamemory_1_dataout));
  Multiplexer #(.select(2), .width(24), .enable("false")) multiplexer_6 (
    .in0(alu_1_result), .in1(datamemory_1_dataout), .in2(adder_1_out), .in3(shifter_1_out),
    .out(multiplexer_6_out), .sel(WBData));
  // Probe on WBData

  // Notes on the sheet:
  //   Imm(17)
  //   Imm(10)
  //   rs
  //   rt
  //   rd
  //   op
  //   sf
  //   cond
endmodule

module RegisterFile (
  input  [23:0] BusW,
  input  [2:0] RA,
  input  [2:0] RW,
  input  [2:0] RB,
  input  RegWR,
  input  clk,
  output [23:0] BusA,
  output [23:0] BusB
);

  wire and_1_out, and_2_out, and_3_out, and_4_out, and_5_out, and_6_out, and_7_out, decoder_1_out1,
       decoder_1_out2, decoder_1_out3, decoder_1_out4, decoder_1_out5, decoder_1_out6, decoder_1_out7;
  wire [23:0] register_1_q, register_2_q, register_3_q, register_4_q, register_5_q, register_6_q,
       register_7_q;

  Decoder #(.select(3), .enable("false")) decoder_1 (
    .out1(decoder_1_out1), .out2(decoder_1_out2), .out3(decoder_1_out3), .out4(decoder_1_out4),
    .out5(decoder_1_out5), .out6(decoder_1_out6), .out7(decoder_1_out7), .sel(RW));  // open: out0
  and and_1 (and_1_out, decoder_1_out1, RegWR);
  and and_2 (and_2_out, decoder_1_out2, RegWR);
  and and_3 (and_3_out, decoder_1_out3, RegWR);
  and and_4 (and_4_out, decoder_1_out4, RegWR);
  and and_5 (and_5_out, decoder_1_out5, RegWR);
  and and_6 (and_6_out, decoder_1_out6, RegWR);
  and and_7 (and_7_out, decoder_1_out7, RegWR);
  Register #(.width(24)) register_1 (.D(BusW), .en(and_1_out), .Q(register_1_q), .clk(clk));  // open: clr
  Register #(.width(24)) register_2 (.D(BusW), .en(and_2_out), .Q(register_2_q), .clk(clk));  // open: clr
  Register #(.width(24)) register_3 (.D(BusW), .en(and_3_out), .Q(register_3_q), .clk(clk));  // open: clr
  Register #(.width(24)) register_4 (.D(BusW), .en(and_4_out), .Q(register_4_q), .clk(clk));  // open: clr
  Register #(.width(24)) register_5 (.D(BusW), .en(and_5_out), .Q(register_5_q), .clk(clk));  // open: clr
  Register #(.width(24)) register_6 (.D(BusW), .en(and_6_out), .Q(register_6_q), .clk(clk));  // open: clr
  Register #(.width(24)) register_7 (.D(BusW), .en(and_7_out), .Q(register_7_q), .clk(clk));  // open: clr
  Multiplexer #(.select(3), .width(24)) multiplexer_1 (
    .in0({24{1'b0}}), .in1(register_1_q), .in2(register_2_q), .in3(register_3_q), .in4(register_4_q),
    .in5(register_5_q), .in6(register_6_q), .in7(register_7_q), .out(BusA), .sel(RA));  // open: en
  Multiplexer #(.select(3), .width(24)) multiplexer_2 (
    .in0({24{1'b0}}), .in1(register_1_q), .in2(register_2_q), .in3(register_3_q), .in4(register_4_q),
    .in5(register_5_q), .in6(register_6_q), .in7(register_7_q), .out(BusB), .sel(RB));  // open: en
endmodule

module InstructionMemory (
  input  [23:0] Address,
  input  clk,
  output [23:0] Instruction
);

  wire not_1_out;
  wire [23:0] divider_1_out;

  not not_1 (not_1_out, clk);
  Divider #(.width(24)) divider_1 (.a(Address), .b(24'h3), .out(divider_1_out));  // open: upper, rem
  RAM #(.addrWidth(24), .dataWidth(24), .bus("separate")) ram_1 (
    .addr(divider_1_out), .data(Instruction), .str(1'b0), .sel(1'b1), .clk(not_1_out), .ld(1'b1), .clr(1'b0));  // open: din
endmodule

module DataMemory (
  input  [23:0] Address,
  input  [23:0] DataIn,
  input  clk,
  input  MemRD,
  input  MemWR,
  output [23:0] DataOut
);

  RAM #(.addrWidth(24), .dataWidth(24), .bus("separate")) ram_1 (
    .addr(Address), .din(DataIn), .data(DataOut), .str(MemWR), .sel(1'b1), .clk(clk), .ld(MemRD));  // open: clr
endmodule

module Extender (
  input  [9:0] DataIn,
  input  ExtOp,
  output [23:0] DataOut
);

  and and_1 (DataOut[23], DataIn[9], ExtOp);

  assign DataOut[22:0] = {{13{DataOut[23]}}, DataIn};
endmodule

module Extender_17 (
  input  [16:0] DataIn,
  output [23:0] DataOut
);

  assign DataOut = {{7{DataIn[16]}}, DataIn};  // Bit_Extender bit_extender_1
endmodule
